// Digital circuit And16.dig as structural Verilog
module And16 (
  input  a_0,
  input  b_0,
  input  a_1,
  input  b_1,
  input  a_2,
  input  b_2,
  input  a_3,
  input  b_3,
  input  a_4,
  input  b_4,
  input  a_5,
  input  b_5,
  input  a_6,
  input  b_6,
  input  a_7,
  input  b_7,
  input  a_8,
  input  b_8,
  input  a_9,
  input  b_9,
  input  a_10,
  input  b_10,
  input  a_11,
  input  b_11,
  input  a_12,
  input  b_12,
  input  a_13,
  input  b_13,
  input  a_14,
  input  b_14,
  input  a_15,
  input  b_15,
  output out_2,
  output out_5,
  output out_8,
  output out_11,
  output out_14,
  output out_17,
  output out_20,
  output out_23,
  output out_26,
  output out_29,
  output out_32,
  output out_35,
  output out_38,
  output out_41,
  output out_44,
  output out_47
);

  and and_1 (out_2, a_0, b_0);
  and and_2 (out_5, a_1, b_1);
  and and_3 (out_8, a_2, b_2);
  and and_4 (out_11, a_3, b_3);
  and and_5 (out_14, a_4, b_4);
  and and_6 (out_17, a_5, b_5);
  and and_7 (out_20, a_6, b_6);
  and and_8 (out_23, a_7, b_7);
  and and_9 (out_26, a_8, b_8);
  and and_10 (out_29, a_9, b_9);
  and and_11 (out_32, a_10, b_10);
  and and_12 (out_35, a_11, b_11);
  and and_13 (out_38, a_12, b_12);
  and and_14 (out_41, a_13, b_13);
  and and_15 (out_44, a_14, b_14);
  and and_16 (out_47, a_15, b_15);
endmodule
