// Digital circuit DMux4Way.dig as structural Verilog
module DMux4Way (
  input  in,
  input  sel_pin1,
  input  sen_pin0,
  output a,
  output b,
  output c,
  output d
);

  wire demultiplexer_1_out_0, demultiplexer_1_out_1;

  Demultiplexer demultiplexer_1 (.sel(sen_pin0), .in(in), .out_0(demultiplexer_1_out_0), .out_1(demultiplexer_1_out_1));
  Demultiplexer demultiplexer_2 (.sel(sel_pin1), .in(demultiplexer_1_out_0), .out_0(a), .out_1(b));
  Demultiplexer demultiplexer_3 (.sel(sel_pin1), .in(demultiplexer_1_out_1), .out_0(c), .out_1(d));
endmodule
