// Digital circuit DMux8Way.dig as structural Verilog
module DMux8Way (
  input  in,
  input  [2:0] sel,
  output a,
  output e,
  output c,
  output g,
  output b,
  output f,
  output d,
  output h
);

  wire bussplitter_1_d0, bussplitter_1_d1, bussplitter_1_d2, dipswitch_1_out, dipswitch_2_out, dmux_1_a,
       dmux_1_b;
  wire [1:0] bussplitter_2_d;

  BusSplitter #(.Bits(3)) bussplitter_1 (
    .D(sel), .OE(dipswitch_1_out), .D0(bussplitter_1_d0), .D1(bussplitter_1_d1), .D2(bussplitter_1_d2));
  DipSwitch #(.dipDefault("true")) dipswitch_1 (.out(dipswitch_1_out));
  Dmux dmux_1 (.in(in), .sel(bussplitter_1_d0), .a(dmux_1_a), .b(dmux_1_b));
  BusSplitter #(.Bits(2)) bussplitter_2 (
    .D(bussplitter_2_d), .OE(dipswitch_2_out), .D0(bussplitter_1_d1), .D1(bussplitter_1_d2));
  DipSwitch dipswitch_2 (.out(dipswitch_2_out));
  DMux4Way dmux4way_1 (.in(dmux_1_a), .sel(bussplitter_2_d), .a(a), .c(e), .b(c), .d(g));
  DMux4Way dmux4way_2 (.in(dmux_1_b), .sel(bussplitter_2_d), .a(b), .c(f), .b(d), .d(h));
endmodule
