// Digital circuit Dmux.dig as structural Verilog
module Dmux (
  input  in,
  input  sel,
  output a,
  output b
);

  wire false_out;

  Button false (.out(false_out));
  Mux mux_1 (.A(in), .B(false_out), .SEL(sel), .Y(a));
  Mux mux_2 (.A(false_out), .B(in), .SEL(sel), .Y(b));
endmodule
