// Digital circuit Mux16.dig as structural Verilog
module Mux16 (
  input  sel,
  input  [15:0] a,
  input  [15:0] b,
  output [15:0] out
);

  wire bussplitter_1_d0, bussplitter_1_d1, bussplitter_1_d2, bussplitter_1_d3, bussplitter_1_d4,
       bussplitter_1_d5, bussplitter_1_d6, bussplitter_1_d7, bussplitter_1_d8, bussplitter_1_d9,
       bussplitter_1_d10, bussplitter_1_d11, bussplitter_1_d12, bussplitter_1_d13, bussplitter_1_d14,
       bussplitter_1_d15, bussplitter_2_d0, bussplitter_2_d1, bussplitter_2_d2, bussplitter_2_d3,
       bussplitter_2_d4, bussplitter_2_d5, bussplitter_2_d6, bussplitter_2_d7, bussplitter_2_d8,
       bussplitter_2_d9, bussplitter_2_d10, bussplitter_2_d11, bussplitter_2_d12, bussplitter_2_d13,
       bussplitter_2_d14, bussplitter_2_d15, dipswitch_1_out, dipswitch_2_out, dipswitch_3_out, mux_1_out,
       mux_2_out, mux_3_out, mux_4_out, mux_5_out, mux_6_out, mux_7_out, mux_8_out, mux_9_out, mux_10_out,
       mux_11_out, mux_12_out, mux_13_out, mux_14_out, mux_15_out, mux_16_out;

  BusSplitter #(.Bits(16)) bussplitter_1 (
    .D(b), .OE(dipswitch_1_out), .D0(bussplitter_1_d0), .D1(bussplitter_1_d1), .D2(bussplitter_1_d2),
    .D3(bussplitter_1_d3), .D4(bussplitter_1_d4), .D5(bussplitter_1_d5), .D6(bussplitter_1_d6),
    .D7(bussplitter_1_d7), .D8(bussplitter_1_d8), .D9(bussplitter_1_d9), .D10(bussplitter_1_d10),
    .D11(bussplitter_1_d11), .D12(bussplitter_1_d12), .D13(bussplitter_1_d13), .D14(bussplitter_1_d14),
    .D15(bussplitter_1_d15));
  DipSwitch #(.dipDefault("true")) dipswitch_1 (.out(dipswitch_1_out));
  BusSplitter #(.Bits(16)) bussplitter_2 (
    .D(a), .OE(dipswitch_2_out), .D0(bussplitter_2_d0), .D1(bussplitter_2_d1), .D2(bussplitter_2_d2),
    .D3(bussplitter_2_d3), .D4(bussplitter_2_d4), .D5(bussplitter_2_d5), .D6(bussplitter_2_d6),
    .D7(bussplitter_2_d7), .D8(bussplitter_2_d8), .D9(bussplitter_2_d9), .D10(bussplitter_2_d10),
    .D11(bussplitter_2_d11), .D12(bussplitter_2_d12), .D13(bussplitter_2_d13), .D14(bussplitter_2_d14),
    .D15(bussplitter_2_d15));
  DipSwitch #(.dipDefault("true")) dipswitch_2 (.out(dipswitch_2_out));
  Mux mux_1 (.a(bussplitter_2_d0), .b(bussplitter_1_d0), .SEL(sel), .out(mux_1_out));
  Mux mux_2 (.a(bussplitter_2_d1), .b(bussplitter_1_d1), .SEL(sel), .out(mux_2_out));
  Mux mux_3 (.a(bussplitter_2_d2), .b(bussplitter_1_d2), .SEL(sel), .out(mux_3_out));
  Mux mux_4 (.a(bussplitter_2_d3), .b(bussplitter_1_d3), .SEL(sel), .out(mux_4_out));
  Mux mux_5 (.a(bussplitter_2_d4), .b(bussplitter_1_d4), .SEL(sel), .out(mux_5_out));
  Mux mux_6 (.a(bussplitter_2_d5), .b(bussplitter_1_d5), .SEL(sel), .out(mux_6_out));
  Mux mux_7 (.a(bussplitter_2_d6), .b(bussplitter_1_d6), .SEL(sel), .out(mux_7_out));
  Mux mux_8 (.a(bussplitter_2_d7), .b(bussplitter_1_d7), .SEL(sel), .out(mux_8_out));
  Mux mux_9 (.a(bussplitter_2_d8), .b(bussplitter_1_d8), .SEL(sel), .out(mux_9_out));
  Mux mux_10 (.a(bussplitter_2_d9), .b(bussplitter_1_d9), .SEL(sel), .out(mux_10_out));
  Mux mux_11 (.a(bussplitter_2_d10), .b(bussplitter_1_d10), .SEL(sel), .out(mux_11_out));
  Mux mux_12 (.a(bussplitter_2_d11), .b(bussplitter_1_d11), .SEL(sel), .out(mux_12_out));
  Mux mux_13 (.a(bussplitter_2_d12), .b(bussplitter_1_d12), .SEL(sel), .out(mux_13_out));
  Mux mux_14 (.a(bussplitter_2_d13), .b(bussplitter_1_d13), .SEL(sel), .out(mux_14_out));
  Mux mux_15 (.a(bussplitter_2_d14), .b(bussplitter_1_d14), .SEL(sel), .out(mux_15_out));
  Mux mux_16 (.a(bussplitter_2_d15), .b(bussplitter_1_d15), .SEL(sel), .out(mux_16_out));
  BusSplitter #(.Bits(16)) bussplitter_3 (
    .D(out), .OE(dipswitch_3_out), .D0(mux_1_out), .D1(mux_2_out), .D2(mux_3_out), .D3(mux_4_out),
    .D4(mux_5_out), .D5(mux_6_out), .D6(mux_7_out), .D7(mux_8_out), .D8(mux_9_out), .D9(mux_10_out),
    .D10(mux_11_out), .D11(mux_12_out), .D12(mux_13_out), .D13(mux_14_out), .D14(mux_15_out), .D15(mux_16_out));
  DipSwitch dipswitch_3 (.out(dipswitch_3_out));
endmodule
