// Digital circuit Mux4Way16.dig as structural Verilog
module Mux4Way16 (
  input  [15:0] a,
  input  [15:0] c,
  input  [15:0] b,
  input  [15:0] d,
  input  [1:0] sel,
  output [15:0] out
);

  wire bussplitter_1_d0, bussplitter_1_d1, dipswitch_1_out, mux16_1_p4, mux16_2_p4;

  DipSwitch #(.dipDefault("true")) dipswitch_1 (.out(dipswitch_1_out));
  BusSplitter #(.Bits(2)) bussplitter_1 (.D(sel), .OE(dipswitch_1_out), .D0(bussplitter_1_d0), .D1(bussplitter_1_d1));
  // Mux16 mux16_1: pin names not known; wires that end beside it: bussplitter_1_d0, a, b, mux16_1_p4
  // Mux16 mux16_2: pin names not known; wires that end beside it: bussplitter_1_d0, c, d, mux16_2_p4
  // Mux16 mux16_3: pin names not known; wires that end beside it: bussplitter_1_d1, mux16_1_p4, mux16_2_p4, out
endmodule
