// Digital circuit Mux8Way16.dig as structural Verilog
module Mux8Way16 (
  input  [15:0] a,
  input  [15:0] b,
  input  [15:0] c,
  input  [15:0] d,
  input  [15:0] e,
  input  [15:0] f,
  input  [15:0] g,
  input  [15:0] h,
  input  [1:0] sel_pin1_e_2,
  input  sel_pin3,
  output [15:0] out
);

  wire [15:0] multiplexer_1_out, multiplexer_2_out;

  Multiplexer #(.Selector_Bits(2), .Bits(16)) multiplexer_1 (
    .sel(sel_pin1_e_2), .in_0(a), .in_1(b), .in_2(c), .in_3(d), .out(multiplexer_1_out));
  Multiplexer #(.Selector_Bits(2), .Bits(16)) multiplexer_2 (
    .sel(sel_pin1_e_2), .in_0(e), .in_1(f), .in_2(g), .in_3(h), .out(multiplexer_2_out));
  Multiplexer #(.Bits(16)) multiplexer_3 (
    .sel(sel_pin3), .in_0(multiplexer_1_out), .in_1(multiplexer_2_out), .out(out));
endmodule
