// Digital circuit Not16.dig as structural Verilog
module Not16 (
  input  pin_0,
  input  pin_1,
  input  pin_2,
  input  pin_3,
  input  pin_4,
  input  pin_5,
  input  pin_6,
  input  pin_7,
  input  pin_8,
  input  pin_9,
  input  pin_10,
  input  pin_11,
  input  pin_12,
  input  pin_13,
  input  pin_14,
  input  pin_15,
  output out_17,
  output out_18,
  output out_19,
  output out_20,
  output out_21,
  output out_22,
  output out_23,
  output out_24,
  output out_25,
  output out_26,
  output out_27,
  output out_28,
  output out_29,
  output out_30,
  output out_31,
  output out_32
);

  nand nand_1 (out_17, pin_0, pin_0);
  nand nand_2 (out_18, pin_1, pin_1);
  nand nand_3 (out_19, pin_2, pin_2);
  nand nand_4 (out_20, pin_3, pin_3);
  nand nand_5 (out_21, pin_4, pin_4);
  nand nand_6 (out_22, pin_5, pin_5);
  nand nand_7 (out_23, pin_6, pin_6);
  nand nand_8 (out_24, pin_7, pin_7);
  nand nand_9 (out_25, pin_8, pin_8);
  nand nand_10 (out_26, pin_9, pin_9);
  nand nand_11 (out_27, pin_10, pin_10);
  nand nand_12 (out_28, pin_11, pin_11);
  nand nand_13 (out_29, pin_12, pin_12);
  nand nand_14 (out_30, pin_13, pin_13);
  nand nand_15 (out_31, pin_14, pin_14);
  nand nand_16 (out_32, pin_15, pin_15);
endmodule
