// Digital circuit Or8Way.dig as structural Verilog
module Or8Way (
  input  in_0,
  input  in_1,
  input  in_2,
  input  in_3,
  input  in_4,
  input  in_5,
  input  in_6,
  input  in_7
);

  wire or_1_out, or_2_out, or_3_out, or_4_out, or_5_out, or_6_out, or_7_out;

  or or_1 (or_1_out, in_0, in_1);
  or or_2 (or_2_out, or_1_out, in_2);
  or or_3 (or_3_out, or_2_out, in_3);
  or or_4 (or_4_out, or_3_out, in_4);
  or or_5 (or_5_out, or_4_out, in_5);
  or or_6 (or_6_out, or_5_out, in_6);
  or or_7 (or_7_out, or_6_out, in_7);
  LED led_1 (.in(or_7_out));
endmodule
